# Fritzing sketch Schetch (saved by Fritzing 0.9.3b)
breadboards: 1

parts:
  Part1 = Arduino Uno (Rev3)
  S1 = Toggle Switch [package=THT]
  Part2 = BME280 Breakout
  Pololu_A1 = Pololu A4988 [package=SO16]
  M1 = Stepper Motor - Bipolar
  R1 = Resistor [tolerance=±5% resistance=220 package="0402 [SMD]"]
  24V_-_DC_power_supply = Battery
  C1 = Capacitor Polarized [package=cpol-radial-10uf-25v]
  X1 = DB15 Connector [package=db15]  # not connected

nets (from the breadboard view):
  N1: Part1.A4/SDA, Part2.SDI/SDA
  N2: Part1.A5/SCL, Part2.SCK/SCL
  N3: Part1.D8, S1.L1, R1.Pin_1
  GND: Part1.GND, S1.COM, Part2.GND, Pololu_A1.GND#8
  N4: Part1.D2, Pololu_A1.DIR
  N5: Part1.D3_PWM, Pololu_A1.STEP
  N6: Part1.D5_PWM, Pololu_A1.ENABLE
  5V: Part1.5V, Part2.3.3V, Pololu_A1.VDD, R1.Pin_0
  N7: Pololu_A1.1B, M1.D
  N8: Pololu_A1.1A, M1.B
  N9: Pololu_A1.2A, M1.C
  N10: Pololu_A1.2B, M1.A
  N11: Pololu_A1.GND#14, 24V_-_DC_power_supply.-, C1.-
  N12: Pololu_A1.VMOT, 24V_-_DC_power_supply.+, C1.+

custom parts:
  DB15 Connector: DB15 Connector Standard DB15 (D-Sub 15) pc midi or gameport connector. Can be used for old PC compatible joystic.
